# Fritzing sketch StrikeAndDip (saved by Fritzing 0.9.3b)
circuit board: 5.1cm x 8.3cm
breadboards: 1

parts:
  Part2 = Adafruit Ultimate GPS v3 [part_number="Adafruit #746"]
  Part3 = MPL3115A2 I2C Barometric Pressure, Altitude, Temperature Sensor
  Part4 = Adafruit LSM9DS1 9DoF Breakout [part_number="Adafruit #3387"]
  Part5 = Adafruit Feather M0 Adalogger [part_number="Adafruit #2796"]
  Part6 = Adafruit OLED FeatherWing [part_number="Adafruit #2900"]

nets:
  GND: Part2.GND, Part3.GND, Part4.GND, Part5.GND, Part6.GND, Part6.G
  N1: Part2.RX, Part5.D1, Part6.TX
  N2: Part2.TX, Part5.D0, Part6.RX
  3.3V: Part2.3.3V, Part3.+3V3, Part4.VIN, Part5.+3V3, Part6.3.3V
  N3: Part3.SCL, Part4.SCL, Part5.SCL, Part6.SCL
  N4: Part3.SDA, Part4.SDA, Part5.SDA, Part6.SDA
  N5: Part5.MISO, Part6.MISO
  N6: Part5.MOSI, Part6.MOSI
  N7: Part5.SCK, Part6.SCK
  N8: Part5.A5, Part6.F
  N9: Part5.A4, Part6.E
  N10: Part5.A3, Part6.D
  N11: Part5.A2, Part6.C
  N12: Part5.A1, Part6.B
  N13: Part5.A0, Part6.A
  N14: Part5.AREF, Part6.AREF
  N15: Part5.!RESET, Part6.!RESET
  N16: Part5.VBAT, Part6.VBAT
  N17: Part5.EN, Part6.EN
  N18: Part5.VBUS, Part6.USB
  N19: Part5.D13, Part6.N
  N20: Part5.D12, Part6.M
  N21: Part5.D11, Part6.L
  N22: Part5.D10, Part6.K
  N23: Part5.D9, Part6.J
  N24: Part5.D6, Part6.I
  N25: Part5.D5, Part6.H

custom parts:
  Adafruit Ultimate GPS v3: We carry a few different GPS modules here in the Adafruit shop, but none that satisfied our every desire - that's why we designed this little GPS breakout board. We believe this is the Ultimate GPS module, so we named it that. It's got everything you want and more: -165 dBm sensitivity, 10 Hz updates, 66 channels 5V friendly design and only 20mA current draw Breadboard friendly + two mounting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
  MPL3115A2 I2C Barometric Pressure, Altitude, Temperature Sensor: This pressure sensor from Freescale is a great low-cost sensing solution for precision measurement of barometric pressure and altitude. The MPL3115A2 has a typical 1.5 Pascal resolution, which can resolve altitude at 0.3 meters (compare to the BMP180 which can do 0.17m). It has some upsides compared to the BMP180, such as interrupt outputs for ultra-low power usage, and its also a heck of a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
  Adafruit LSM9DS1 9DoF Breakout: Add motion, direction and orientation sensing to your Arduino project with this all-in-one 9-DOF sensor. Inside the chip are three sensors, one is a classic 3-axis accelerometer, which can tell you which direction is down towards the Earth (by measuring gravity) or how fast the board is accelerating in 3D space. The other is a 3-axis magnetometer that can sense where the strongest magnetic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
  Adafruit Feather M0 Adalogger: This is the Adafruit Feather M0 Adalogger - our take on an 'all-in-one' Cortex M0 datalogger (or data-reader) with built in USB and battery charging. Its an Adafruit Feather M0 with a microSD holder ready to rock! We have other boards in the Feather family, check'em out here At the Feather M0's heart is an ATSAMD21G18 ARM Cortex M0 processor, clocked at 48 MHz and at 3.3V logic, the same one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
  Adafruit OLED FeatherWing: This is the FeatherWing OLED: it adds a 128x32 monochrome OLED plus 3 user buttons to any Feather main board. These displays are small, only about 1" diagonal, but very readable due to the high contrast of an OLED display. This screen is made of 128x32 individual white OLED pixels and because the display makes its own light, no backlight is required. This reduces the power required to run the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
